// Logisim project ALU.circ as structural Verilog
module my_adder (
  input  A,
  input  B,
  output SUM,
  output CARRY
);

  xor xor_1 (SUM, A, B);
  and and_1 (CARRY, A, B);
endmodule

module full_adder (
  input  A,
  input  B,
  input  CIN,
  output SUM,
  output COUT
);

  wire and_1_out, and_2_out, xor_1_out;

  xor xor_1 (xor_1_out, A, B);
  and and_1 (and_1_out, A, B);
  and and_2 (and_2_out, xor_1_out, CIN);
  xor xor_2 (SUM, xor_1_out, CIN);
  or or_1 (COUT, and_2_out, and_1_out);
endmodule

module full_4bit_adder (
  input  CIN,
  input  A1,
  input  A2,
  input  A3,
  input  A4,
  input  B1,
  input  B2,
  input  B3,
  input  B4,
  output S1,
  output S2,
  output S3,
  output S4,
  output COUT
);

  wire full_adder_1_cout, full_adder_2_cout, full_adder_3_cout;

  full_adder full_adder_1 (.A(A1), .B(B1), .CIN(CIN), .SUM(S1), .COUT(full_adder_1_cout));
  full_adder full_adder_2 (.A(A2), .B(B2), .CIN(full_adder_1_cout), .SUM(S2), .COUT(full_adder_2_cout));
  full_adder full_adder_3 (.A(A3), .B(B3), .CIN(full_adder_2_cout), .SUM(S3), .COUT(full_adder_3_cout));
  full_adder full_adder_4 (.A(A4), .B(B4), .CIN(full_adder_3_cout), .SUM(S4), .COUT(COUT));
endmodule
